// Logisim project flappy_bird -4.05.2026.circ as structural Verilog
module main (
  input  PAUSE
);

  wire \break , break_1_break, break_2_break, clock_1_out, counter_1_carry, not_1_out, or_1_out,
       pipes_lfsr_1_out_6, res, tacts, \КНОПКА_out ;
  wire [3:0] counter_1_q, counter_2_q;
  wire [7:0] counter_3_q;
  wire [31:0] bird_1_out_6, bird_1_out_7, bird_1_out_8, bird_1_out_9, bird_1_out_10, min, movement_1_bird_a,
       movement_1_bird_b, movement_1_out_9, movement_1_out_10, movement_1_out_13, movement_1_out_14,
       movement_1_out_17, pipes_lfsr_1_out_4, pipes_lfsr_1_out_5, pipes_lfsr_1_out_7, pipes_lfsr_1_out_8,
       pipes_lfsr_1_out_9, pipes_lfsr_1_out_10, pipes_lfsr_1_out_11, pipes_lfsr_1_out_12,
       pipes_lfsr_1_out_13, pipes_lfsr_1_out_14, pipes_lfsr_1_out_15, pipes_lfsr_1_out_16,
       pipes_lfsr_1_out_17, pipes_lfsr_1_out_18, pipes_lfsr_1_out_19, pipes_lfsr_1_out_20,
       pipes_lfsr_1_out_21, pipes_lfsr_1_out_22, pipes_lfsr_1_out_23, pipes_lfsr_1_out_24,
       pipes_lfsr_1_out_25, pipes_lfsr_1_out_26, pipes_lfsr_1_out_27, pipes_lfsr_1_out_28,
       pipes_lfsr_1_out_29, pipes_lfsr_1_out_30, pipes_lfsr_1_out_31, pipes_lfsr_1_out_32,
       pipes_lfsr_1_out_33, pipes_lfsr_1_out_34, pipes_lfsr_1_out_35, pipes_lfsr_1_out_36, screen_1_out_34,
       screen_1_out_35, screen_1_out_36, screen_1_out_37, screen_1_out_38, screen_1_out_39, screen_1_out_40,
       screen_1_out_41, screen_1_out_42, screen_1_out_43, screen_1_out_44, screen_1_out_45, screen_1_out_46,
       screen_1_out_47, screen_1_out_48, screen_1_out_49, screen_1_out_50, screen_1_out_51, screen_1_out_52,
       screen_1_out_53, screen_1_out_54, screen_1_out_55, screen_1_out_56, screen_1_out_57, screen_1_out_58,
       screen_1_out_59, screen_1_out_60, screen_1_out_61, screen_1_out_62, screen_1_out_63, screen_1_out_64,
       screen_1_out_65;

  Clock clock_1 (.out(clock_1_out));
  or or_1 (or_1_out, \break , PAUSE);
  Button \u_СБРОС  (.out(res));
  Button \u_КНОПКА  (.out(\КНОПКА_out ));
  and and_1 (tacts, clock_1_out, not_1_out);
  not not_1 (not_1_out, or_1_out);
  DotMatrix #(.matrixcols(32), .matrixrows(32)) dotmatrix_1 (
    .col0(screen_1_out_34), .col1(screen_1_out_35), .col2(screen_1_out_36), .col3(screen_1_out_37),
    .col4(screen_1_out_38), .col5(screen_1_out_39), .col6(screen_1_out_40), .col7(screen_1_out_41),
    .col8(screen_1_out_42), .col9(screen_1_out_43), .col10(screen_1_out_44), .col11(screen_1_out_45),
    .col12(screen_1_out_46), .col13(screen_1_out_47), .col14(screen_1_out_48), .col15(screen_1_out_49),
    .col16(screen_1_out_50), .col17(screen_1_out_51), .col18(screen_1_out_52), .col19(screen_1_out_53),
    .col20(screen_1_out_54), .col21(screen_1_out_55), .col22(screen_1_out_56), .col23(screen_1_out_57),
    .col24(screen_1_out_58), .col25(screen_1_out_59), .col26(screen_1_out_60), .col27(screen_1_out_61),
    .col28(screen_1_out_62), .col29(screen_1_out_63), .col30(screen_1_out_64), .col31(screen_1_out_65));
  Screen screen_1 (
    .in_33(\break ), .out_34(screen_1_out_34), .out_35(screen_1_out_35), .out_36(screen_1_out_36),
    .out_37(screen_1_out_37), .out_38(screen_1_out_38), .out_39(screen_1_out_39), .out_40(screen_1_out_40),
    .out_41(screen_1_out_41), .out_42(screen_1_out_42), .out_43(screen_1_out_43), .out_44(screen_1_out_44),
    .out_45(screen_1_out_45), .out_46(screen_1_out_46), .out_47(screen_1_out_47), .out_48(screen_1_out_48),
    .out_49(screen_1_out_49), .out_50(screen_1_out_50), .out_51(screen_1_out_51), .out_52(screen_1_out_52),
    .out_53(screen_1_out_53), .out_54(screen_1_out_54), .out_55(screen_1_out_55), .out_56(screen_1_out_56),
    .out_57(screen_1_out_57), .out_58(screen_1_out_58), .out_59(screen_1_out_59), .out_60(screen_1_out_60),
    .out_61(screen_1_out_61), .out_62(screen_1_out_62), .out_63(screen_1_out_63), .out_64(screen_1_out_64),
    .out_65(screen_1_out_65), .in_1(pipes_lfsr_1_out_7), .in_2(pipes_lfsr_1_out_8),
    .in_3(pipes_lfsr_1_out_4), .in_4(movement_1_out_9), .in_5(movement_1_out_10), .in_6(movement_1_out_14),
    .in_7(movement_1_out_17), .in_8(movement_1_out_13), .in_9(pipes_lfsr_1_out_13),
    .in_10(pipes_lfsr_1_out_14), .in_11(pipes_lfsr_1_out_15), .in_12(pipes_lfsr_1_out_16),
    .in_13(pipes_lfsr_1_out_17), .in_14(pipes_lfsr_1_out_18), .in_15(pipes_lfsr_1_out_19),
    .in_16(pipes_lfsr_1_out_20), .in_17(pipes_lfsr_1_out_21), .in_18(pipes_lfsr_1_out_22),
    .in_19(pipes_lfsr_1_out_23), .in_20(pipes_lfsr_1_out_24), .in_21(pipes_lfsr_1_out_25),
    .in_22(pipes_lfsr_1_out_26), .in_23(pipes_lfsr_1_out_27), .in_24(pipes_lfsr_1_out_28),
    .in_25(pipes_lfsr_1_out_29), .in_26(pipes_lfsr_1_out_30), .in_27(pipes_lfsr_1_out_31),
    .in_28(pipes_lfsr_1_out_32), .in_29(pipes_lfsr_1_out_33), .in_30(pipes_lfsr_1_out_34),
    .in_31(pipes_lfsr_1_out_35), .in_32(pipes_lfsr_1_out_36));
  movement movement_1 (
    .in_1(bird_1_out_7), .in_7(bird_1_out_8), .out_10(movement_1_out_10), .\Прыжок (\КНОПКА_out ), .res(res),
    .\Такты (tacts), .out_14(movement_1_out_14), .bird_b(movement_1_bird_b), .bird_a(movement_1_bird_a),
    .in_8(bird_1_out_9), .in_2(bird_1_out_6), .out_9(movement_1_out_9), .in_6(bird_1_out_10),
    .out_13(movement_1_out_13), .out_17(movement_1_out_17));  // open: bird_d, bird_c, bird_e
  bird bird_1 (
    .out_7(bird_1_out_7), .out_8(bird_1_out_8), .bird_a(pipes_lfsr_1_out_9), .bird_b(pipes_lfsr_1_out_10),
    .out_9(bird_1_out_9), .bird_c(pipes_lfsr_1_out_11), .out_6(bird_1_out_6), .bird_e(pipes_lfsr_1_out_5),
    .out_10(bird_1_out_10), .bird_e_2(pipes_lfsr_1_out_12));
  pipes_lfsr pipes_lfsr_1 (
    .reset(res), .in(min), .out_6(pipes_lfsr_1_out_6), .in_1(tacts), .out_7(pipes_lfsr_1_out_7),
    .out_8(pipes_lfsr_1_out_8), .out_4(pipes_lfsr_1_out_4), .out_5(pipes_lfsr_1_out_5),
    .out_9(pipes_lfsr_1_out_9), .out_10(pipes_lfsr_1_out_10), .out_11(pipes_lfsr_1_out_11),
    .out_12(pipes_lfsr_1_out_12), .out_13(pipes_lfsr_1_out_13), .out_14(pipes_lfsr_1_out_14),
    .out_15(pipes_lfsr_1_out_15), .out_16(pipes_lfsr_1_out_16), .out_17(pipes_lfsr_1_out_17),
    .out_18(pipes_lfsr_1_out_18), .out_19(pipes_lfsr_1_out_19), .out_20(pipes_lfsr_1_out_20),
    .out_21(pipes_lfsr_1_out_21), .out_22(pipes_lfsr_1_out_22), .out_23(pipes_lfsr_1_out_23),
    .out_24(pipes_lfsr_1_out_24), .out_25(pipes_lfsr_1_out_25), .out_26(pipes_lfsr_1_out_26),
    .out_27(pipes_lfsr_1_out_27), .out_28(pipes_lfsr_1_out_28), .out_29(pipes_lfsr_1_out_29),
    .out_30(pipes_lfsr_1_out_30), .out_31(pipes_lfsr_1_out_31), .out_32(pipes_lfsr_1_out_32),
    .out_33(pipes_lfsr_1_out_33), .out_34(pipes_lfsr_1_out_34), .out_35(pipes_lfsr_1_out_35),
    .out_36(pipes_lfsr_1_out_36));
  Hex_Digit_Display hex_digit_display_1 (.value(counter_2_q));  // open: dp
  Hex_Digit_Display hex_digit_display_2 (.value(counter_1_q));  // open: dp
  Counter #(.width(4), .max('h9)) counter_1 (
    .Q(counter_1_q), .carry(counter_1_carry), .clk(pipes_lfsr_1_out_6), .clr(res));  // open: load, D, count
  Counter #(.width(4), .max('h9), .trigger("falling")) counter_2 (
    .Q(counter_2_q), .clk(counter_1_carry), .clr(res));  // open: load, D, count, carry
  \break  break_1 (.a(movement_1_bird_b), .b(pipes_lfsr_1_out_9), .\break (break_1_break));
  \break  break_2 (.a(movement_1_bird_a), .b(pipes_lfsr_1_out_10), .\break (break_2_break));
  Counter counter_3 (.Q(counter_3_q), .clk(tacts), .clr(\break ));  // open: load, D, count, carry
  or or_2 (\break , break_1_break, break_2_break);
  ROM #(.dataWidth(32)) rom_1 (.addr(counter_3_q), .data(min));  // open: sel

  // Notes on the sheet:
  //   contents of rom_1 (hex, n*v repeats v):
  //   16*0 ffc07fff ffc07fff 6*0 ffc07fff ffc07fff 6*0 ffc3ffff ffc3ffff 6*0 ffc3ffff ffc3ffff 6*0
  //   ffc1ffff ffc1ffff 6*0 ffc1ffff ffc1ffff 6*0 ffc03fff ffc03fff 6*0 ffc03fff ffc03fff 6*0 ffc0ffff
  //   ffc0ffff 6*0 ffc0ffff ffc0ffff 6*0 ffc01fff ffc01fff 6*0 ffc01fff ffc01fff 6*0 ffc00fff ffc00fff 6*0
  //   ffc00fff ffc00fff 6*0 ffc7ffff ffc7ffff 6*0 ffc7ffff ffc7ffff 6*0 ffc3ffff ffc3ffff 6*0 ffc3ffff
  //   ffc3ffff 6*0 ffc1ffff ffc1ffff 6*0 ffc1ffff ffc1ffff 6*0 ffc07fff ffc07fff 6*0 ffc07fff ffc07fff 6*0
  //   ffc0ffff ffc0ffff 6*0 ffc0ffff ffc0ffff 6*0 ffc03fff ffc03fff 6*0 ffc03fff ffc03fff 6*0 ffc01fff
  //   ffc01fff 6*0 ffc01fff ffc01fff 6*0 ffc7ffff ffc7ffff 4*0 ffc7ffff ffc7ffff 4*0 ffc01fff ffc01fff
endmodule

module Screen (
  input  [31:0] in_1,
  input  [31:0] in_2,
  input  [31:0] in_3,
  input  [31:0] in_4,
  input  [31:0] in_5,
  input  [31:0] in_6,
  input  [31:0] in_7,
  input  [31:0] in_8,
  input  [31:0] in_9,
  input  [31:0] in_10,
  input  [31:0] in_11,
  input  [31:0] in_12,
  input  [31:0] in_13,
  input  [31:0] in_14,
  input  [31:0] in_15,
  input  [31:0] in_16,
  input  [31:0] in_17,
  input  [31:0] in_18,
  input  [31:0] in_19,
  input  [31:0] in_20,
  input  [31:0] in_21,
  input  [31:0] in_22,
  input  [31:0] in_23,
  input  [31:0] in_24,
  input  [31:0] in_25,
  input  [31:0] in_26,
  input  [31:0] in_27,
  input  [31:0] in_28,
  input  [31:0] in_29,
  input  [31:0] in_30,
  input  [31:0] in_31,
  input  [31:0] in_32,
  input  in_33,
  output [31:0] out_34,
  output [31:0] out_35,
  output [31:0] out_36,
  output [31:0] out_37,
  output [31:0] out_38,
  output [31:0] out_39,
  output [31:0] out_40,
  output [31:0] out_41,
  output [31:0] out_42,
  output [31:0] out_43,
  output [31:0] out_44,
  output [31:0] out_45,
  output [31:0] out_46,
  output [31:0] out_47,
  output [31:0] out_48,
  output [31:0] out_49,
  output [31:0] out_50,
  output [31:0] out_51,
  output [31:0] out_52,
  output [31:0] out_53,
  output [31:0] out_54,
  output [31:0] out_55,
  output [31:0] out_56,
  output [31:0] out_57,
  output [31:0] out_58,
  output [31:0] out_59,
  output [31:0] out_60,
  output [31:0] out_61,
  output [31:0] out_62,
  output [31:0] out_63,
  output [31:0] out_64,
  output [31:0] out_65
);

  Multiplexer #(.width(32)) multiplexer_1 (.in0(in_1), .in1({32{1'b0}}), .out(out_34), .sel(in_33));  // open: en
  Multiplexer #(.width(32)) multiplexer_2 (.in0(in_2), .in1({32{1'b0}}), .out(out_35), .sel(in_33));  // open: en
  Multiplexer #(.width(32)) multiplexer_3 (.in0(in_3), .in1({32{1'b0}}), .out(out_36), .sel(in_33));  // open: en
  Multiplexer #(.width(32)) multiplexer_4 (.in0(in_4), .in1(32'h18003ff8), .out(out_37), .sel(in_33));  // open: en
  Multiplexer #(.width(32)) multiplexer_5 (.in0(in_5), .in1(32'h6002008), .out(out_38), .sel(in_33));  // open: en
  Multiplexer #(.width(32)) multiplexer_6 (.in0(in_6), .in1(32'h1802008), .out(out_39), .sel(in_33));  // open: en
  Multiplexer #(.width(32)) multiplexer_7 (.in0(in_7), .in1(32'h7c2008), .out(out_40), .sel(in_33));  // open: en
  Multiplexer #(.width(32)) multiplexer_8 (.in0(in_8), .in1(32'h1802008), .out(out_41), .sel(in_33));  // open: en
  Multiplexer #(.width(32)) multiplexer_9 (.in0(in_9), .in1(32'h6001010), .out(out_42), .sel(in_33));  // open: en
  Multiplexer #(.width(32)) multiplexer_10 (.in0(in_10), .in1(32'h18000fe0), .out(out_43), .sel(in_33));  // open: en
  Multiplexer #(.width(32)) multiplexer_11 (.in0(in_11), .in1({32{1'b0}}), .out(out_44), .sel(in_33));  // open: en
  Multiplexer #(.width(32)) multiplexer_12 (.in0(in_12), .in1({32{1'b0}}), .out(out_45), .sel(in_33));  // open: en
  Multiplexer #(.width(32)) multiplexer_13 (.in0(in_13), .in1(32'h7f03ff8), .out(out_46), .sel(in_33));  // open: en
  Multiplexer #(.width(32)) multiplexer_14 (.in0(in_14), .in1(32'h8080000), .out(out_47), .sel(in_33));  // open: en
  Multiplexer #(.width(32)) multiplexer_15 (.in0(in_15), .in1(32'h10040000), .out(out_48), .sel(in_33));  // open: en
  Multiplexer #(.width(32)) multiplexer_16 (.in0(in_16), .in1(32'h10043ff8), .out(out_49), .sel(in_33));  // open: en
  Multiplexer #(.width(32)) multiplexer_17 (.in0(in_17), .in1(32'h10042108), .out(out_50), .sel(in_33));  // open: en
  Multiplexer #(.width(32)) multiplexer_18 (.in0(in_18), .in1(32'h10042108), .out(out_51), .sel(in_33));  // open: en
  Multiplexer #(.width(32)) multiplexer_19 (.in0(in_19), .in1(32'h8082108), .out(out_52), .sel(in_33));  // open: en
  Multiplexer #(.width(32)) multiplexer_20 (.in0(in_20), .in1(32'h7f02108), .out(out_53), .sel(in_33));  // open: en
  Multiplexer #(.width(32)) multiplexer_21 (.in0(in_21), .in1({32{1'b0}}), .out(out_54), .sel(in_33));  // open: en
  Multiplexer #(.width(32)) multiplexer_22 (.in0(in_22), .in1({32{1'b0}}), .out(out_55), .sel(in_33));  // open: en
  Multiplexer #(.width(32)) multiplexer_23 (.in0(in_23), .in1(32'h1ff03ff8), .out(out_56), .sel(in_33));  // open: en
  Multiplexer #(.width(32)) multiplexer_24 (.in0(in_24), .in1(32'h82008), .out(out_57), .sel(in_33));  // open: en
  Multiplexer #(.width(32)) multiplexer_25 (.in0(in_25), .in1(32'h42008), .out(out_58), .sel(in_33));  // open: en
  Multiplexer #(.width(32)) multiplexer_26 (.in0(in_26), .in1(32'h42008), .out(out_59), .sel(in_33));  // open: en
  Multiplexer #(.width(32)) multiplexer_27 (.in0(in_27), .in1(32'h42008), .out(out_60), .sel(in_33));  // open: en
  Multiplexer #(.width(32)) multiplexer_28 (.in0(in_28), .in1(32'h81010), .out(out_61), .sel(in_33));  // open: en
  Multiplexer #(.width(32)) multiplexer_29 (.in0(in_29), .in1(32'h1ff00fe0), .out(out_62), .sel(in_33));  // open: en
  Multiplexer #(.width(32)) multiplexer_30 (.in0(in_30), .in1({32{1'b0}}), .out(out_63), .sel(in_33));  // open: en
  Multiplexer #(.width(32)) multiplexer_31 (.in0(in_31), .in1({32{1'b0}}), .out(out_64), .sel(in_33));  // open: en
  Multiplexer #(.width(32)) multiplexer_32 (.in0(in_32), .in1({32{1'b0}}), .out(out_65), .sel(in_33));  // open: en

  // Other names for the same wires on the sheet: inp = in_33
endmodule

module bird (
  input  [31:0] bird_e,
  input  [31:0] bird_a,
  input  [31:0] bird_b,
  input  [31:0] bird_c,
  input  [31:0] bird_e_2,
  output [31:0] out_6,
  output [31:0] out_7,
  output [31:0] out_8,
  output [31:0] out_9,
  output [31:0] out_10
);

  assign out_6 = 32'h1000 | bird_e;  // OR_Gate or_1, 32 bits wide
  assign out_7 = 32'h3800 | bird_a;  // OR_Gate or_2, 32 bits wide
  assign out_8 = 32'h3800 | bird_b;  // OR_Gate or_3, 32 bits wide
  assign out_9 = 32'h3800 | bird_c;  // OR_Gate or_4, 32 bits wide
  assign out_10 = 32'h1000 | bird_e_2;  // OR_Gate or_5, 32 bits wide
endmodule

module movement (
  input  [31:0] in_1,
  input  [31:0] in_2,
  input  \Прыжок ,
  input  \Такты ,
  input  res,
  input  [31:0] in_6,
  input  [31:0] in_7,
  input  [31:0] in_8,
  output [31:0] out_9,
  output [31:0] out_10,
  output [31:0] bird_d,
  output [31:0] bird_a,
  output [31:0] out_13,
  output [31:0] out_14,
  output [31:0] bird_e,
  output [31:0] bird_b,
  output [31:0] out_17,
  output [31:0] bird_c
);

  wire comparator_1_gt, comparator_2_gt, comparator_3_gt, comparator_4_gt, comparator_5_gt;
  wire [31:0] and_1_out, and_2_out, and_3_out, and_4_out, and_5_out, counter_1_q, counter_2_q, counter_3_q,
       counter_4_q, counter_5_q, divider_1_out, divider_2_out, divider_3_out, divider_4_out, divider_5_out,
       multiplexer_1_out, multiplexer_2_out, multiplexer_3_out, multiplexer_4_out, multiplexer_5_out,
       multiplexer_6_out, multiplexer_7_out, multiplexer_8_out, multiplexer_9_out, multiplexer_10_out,
       multiplier_1_out, multiplier_2_out, multiplier_3_out, multiplier_4_out, multiplier_5_out;

  Counter #(.width(32), .max('hffffffff)) counter_1 (
    .Q(counter_1_q), .clk(\Такты ), .clr(res));  // open: load, D, count, carry
  Counter #(.width(32), .max('hffffffff)) counter_2 (
    .Q(counter_2_q), .clk(\Такты ), .clr(res));  // open: load, D, count, carry
  Counter #(.width(32), .max('hffffffff)) counter_3 (
    .Q(counter_3_q), .clk(\Такты ), .clr(res));  // open: load, D, count, carry
  assign and_1_out = in_1 & 32'h7ffffffe;  // AND_Gate and_1, 32 bits wide
  Multiplexer #(.width(32)) multiplexer_1 (
    .in0(and_1_out), .in1(bird_a), .out(multiplexer_1_out), .sel(comparator_1_gt));  // open: en
  Comparator #(.width(32)) comparator_1 (.a(counter_2_q), .b(32'h1), .gt(comparator_1_gt));  // open: eq, lt
  assign and_2_out = in_7 & 32'h7ffffffe;  // AND_Gate and_2, 32 bits wide
  Comparator #(.width(32)) comparator_2 (.a(counter_1_q), .b(32'h1), .gt(comparator_2_gt));  // open: eq, lt
  assign and_3_out = in_8 & 32'h7ffffffe;  // AND_Gate and_3, 32 bits wide
  Comparator #(.width(32)) comparator_3 (.a(counter_3_q), .b(32'h1), .gt(comparator_3_gt));  // open: eq, lt
  Multiplexer #(.width(32)) multiplexer_2 (
    .in0(and_2_out), .in1(bird_b), .out(multiplexer_2_out), .sel(comparator_2_gt));  // open: en
  Multiplexer #(.width(32)) multiplexer_3 (
    .in0(and_3_out), .in1(bird_c), .out(multiplexer_3_out), .sel(comparator_3_gt));  // open: en
  Divider #(.width(32)) divider_1 (.a(multiplexer_1_out), .b(32'h2), .out(divider_1_out));  // open: upper, rem
  Multiplier #(.width(32)) multiplier_1 (.a(multiplexer_1_out), .b(32'h2), .out(multiplier_1_out));  // open: cin, cout
  Divider #(.width(32)) divider_2 (.a(multiplexer_2_out), .b(32'h2), .out(divider_2_out));  // open: upper, rem
  Multiplexer #(.width(32)) multiplexer_4 (
    .in0(divider_2_out), .in1(multiplier_2_out), .out(multiplexer_4_out), .sel(\Прыжок ));  // open: en
  Multiplier #(.width(32)) multiplier_2 (.a(multiplexer_2_out), .b(32'h2), .out(multiplier_2_out));  // open: cin, cout
  Divider #(.width(32)) divider_3 (.a(multiplexer_3_out), .b(32'h2), .out(divider_3_out));  // open: upper, rem
  Multiplier #(.width(32)) multiplier_3 (.a(multiplexer_3_out), .b(32'h2), .out(multiplier_3_out));  // open: cin, cout
  Register #(.width(32)) register_1 (.D(multiplexer_5_out), .Q(bird_a), .clk(\Такты ), .clr(res));  // open: en
  Multiplexer #(.width(32)) multiplexer_5 (
    .in0(divider_1_out), .in1(multiplier_1_out), .out(multiplexer_5_out), .sel(\Прыжок ));  // open: en
  Register #(.width(32)) register_2 (.D(multiplexer_4_out), .Q(bird_b), .clk(\Такты ), .clr(res));  // open: en
  Register #(.width(32)) register_3 (.D(multiplexer_6_out), .Q(bird_c), .clk(\Такты ), .clr(res));  // open: en
  Multiplexer #(.width(32)) multiplexer_6 (
    .in0(divider_3_out), .in1(multiplier_3_out), .out(multiplexer_6_out), .sel(\Прыжок ));  // open: en
  assign out_10 = {1'b1, bird_a[30:21], 2'b00, bird_a[18:1], 1'b1} | bird_a;  // OR_Gate or_1, 32 bits wide
  assign out_14 = {1'b1, bird_b[30:21], 2'b00, bird_b[18:1], 1'b1} | bird_b;  // OR_Gate or_2, 32 bits wide
  assign out_17 = {1'b1, bird_c[30:21], 2'b00, bird_c[18:1], 1'b1} | bird_c;  // OR_Gate or_3, 32 bits wide
  Counter #(.width(32), .max('hffffffff)) counter_4 (
    .Q(counter_4_q), .clk(\Такты ), .clr(res));  // open: load, D, count, carry
  assign and_4_out = in_2 & 32'h7ffffffe;  // AND_Gate and_4, 32 bits wide
  Comparator #(.width(32)) comparator_4 (.a(counter_4_q), .b(32'h1), .gt(comparator_4_gt));  // open: eq, lt
  Counter #(.width(32), .max('hffffffff)) counter_5 (
    .Q(counter_5_q), .clk(\Такты ), .clr(res));  // open: load, D, count, carry
  Multiplexer #(.width(32)) multiplexer_7 (
    .in0(and_4_out), .in1(bird_d), .out(multiplexer_7_out), .sel(comparator_4_gt));  // open: en
  assign and_5_out = in_6 & 32'h7ffffffe;  // AND_Gate and_5, 32 bits wide
  Comparator #(.width(32)) comparator_5 (.a(counter_5_q), .b(32'h1), .gt(comparator_5_gt));  // open: eq, lt
  Divider #(.width(32)) divider_4 (.a(multiplexer_7_out), .b(32'h2), .out(divider_4_out));  // open: upper, rem
  Multiplier #(.width(32)) multiplier_4 (.a(multiplexer_7_out), .b(32'h2), .out(multiplier_4_out));  // open: cin, cout
  Multiplexer #(.width(32)) multiplexer_8 (
    .in0(and_5_out), .in1(bird_e), .out(multiplexer_8_out), .sel(comparator_5_gt));  // open: en
  Multiplexer #(.width(32)) multiplexer_9 (
    .in0(divider_4_out), .in1(multiplier_4_out), .out(multiplexer_9_out), .sel(\Прыжок ));  // open: en
  Divider #(.width(32)) divider_5 (.a(multiplexer_8_out), .b(32'h2), .out(divider_5_out));  // open: upper, rem
  Multiplier #(.width(32)) multiplier_5 (.a(multiplexer_8_out), .b(32'h2), .out(multiplier_5_out));  // open: cin, cout
  Register #(.width(32)) register_4 (.D(multiplexer_9_out), .Q(bird_d), .clk(\Такты ), .clr(res));  // open: en
  Multiplexer #(.width(32)) multiplexer_10 (
    .in0(divider_5_out), .in1(multiplier_5_out), .out(multiplexer_10_out), .sel(\Прыжок ));  // open: en
  Register #(.width(32)) register_5 (.D(multiplexer_10_out), .Q(bird_e), .clk(\Такты ), .clr(res));  // open: en
  assign out_9 = {1'b1, bird_d[30:21], 2'b00, bird_d[18:1], 1'b1} | bird_d;  // OR_Gate or_4, 32 bits wide
  assign out_13 = {1'b1, bird_e[30:21], 2'b00, bird_e[18:1], 1'b1} | bird_e;  // OR_Gate or_5, 32 bits wide

  // Other names for the same wires on the sheet: jmp = \Прыжок ; sbros = res; tact = \Такты 
endmodule

module pipes_lfsr (
  input  in_1,
  input  reset,
  input  [31:0] in,
  output [31:0] out_4,
  output [31:0] out_5,
  output out_6,
  output [31:0] out_7,
  output [31:0] out_8,
  output [31:0] out_9,
  output [31:0] out_10,
  output [31:0] out_11,
  output [31:0] out_12,
  output [31:0] out_13,
  output [31:0] out_14,
  output [31:0] out_15,
  output [31:0] out_16,
  output [31:0] out_17,
  output [31:0] out_18,
  output [31:0] out_19,
  output [31:0] out_20,
  output [31:0] out_21,
  output [31:0] out_22,
  output [31:0] out_23,
  output [31:0] out_24,
  output [31:0] out_25,
  output [31:0] out_26,
  output [31:0] out_27,
  output [31:0] out_28,
  output [31:0] out_29,
  output [31:0] out_30,
  output [31:0] out_31,
  output [31:0] out_32,
  output [31:0] out_33,
  output [31:0] out_34,
  output [31:0] out_35,
  output [31:0] out_36
);

  wire luboy_1_out_3, luboy_2_out_3;
  wire [31:0] register_1_q, register_2_q, register_3_q, register_4_q, register_5_q, register_6_q,
       register_7_q, register_8_q, register_9_q, register_10_q, register_11_q, register_12_q, register_13_q,
       register_14_q, register_15_q, register_16_q, register_17_q, register_18_q, register_19_q,
       register_20_q, register_21_q, register_22_q, register_23_q, register_24_q, register_25_q,
       register_26_q, register_27_q, register_28_q, register_29_q, register_30_q, register_31_q,
       register_32_q, register_33_q;

  Register #(.width(32)) register_1 (.D(register_2_q), .Q(register_1_q), .clk(in_1), .clr(reset));  // open: en
  assign out_7 = 32'h80000001 | register_1_q;  // OR_Gate or_1, 32 bits wide
  Register #(.width(32)) register_2 (.D(register_3_q), .Q(register_2_q), .clk(in_1), .clr(reset));  // open: en
  assign out_8 = 32'h80000001 | register_2_q;  // OR_Gate or_2, 32 bits wide
  Register #(.width(32)) register_3 (.D(register_4_q), .Q(register_3_q), .clk(in_1), .clr(reset));  // open: en
  assign out_4 = 32'h80000001 | register_3_q;  // OR_Gate or_3, 32 bits wide
  Register #(.width(32)) register_4 (.D(register_5_q), .Q(register_4_q), .clk(in_1), .clr(reset));  // open: en
  assign out_5 = 32'h80000001 | register_4_q;  // OR_Gate or_4, 32 bits wide
  Register #(.width(32)) register_5 (.D(register_6_q), .Q(register_5_q), .clk(in_1), .clr(reset));  // open: en
  luboy luboy_1 (.a(out_4), .b(out_4), .out_3(luboy_1_out_3));
  and and_1 (out_6, luboy_1_out_3, luboy_2_out_3);
  luboy luboy_2 (.a(out_5), .b(out_5), .out_3(luboy_2_out_3));
  assign out_9 = 32'h80000001 | register_5_q;  // OR_Gate or_5, 32 bits wide
  Register #(.width(32)) register_6 (.D(register_7_q), .Q(register_6_q), .clk(in_1), .clr(reset));  // open: en
  assign out_10 = 32'h80000001 | register_6_q;  // OR_Gate or_6, 32 bits wide
  Register #(.width(32)) register_7 (.D(register_8_q), .Q(register_7_q), .clk(in_1), .clr(reset));  // open: en
  assign out_11 = 32'h80000001 | register_7_q;  // OR_Gate or_7, 32 bits wide
  Register #(.width(32)) register_8 (.D(register_9_q), .Q(register_8_q), .clk(in_1), .clr(reset));  // open: en
  assign out_12 = 32'h80000001 | register_8_q;  // OR_Gate or_8, 32 bits wide
  Register #(.width(32)) register_9 (.D(register_10_q), .Q(register_9_q), .clk(in_1), .clr(reset));  // open: en
  assign out_13 = 32'h80000001 | register_9_q;  // OR_Gate or_9, 32 bits wide
  Register #(.width(32)) register_10 (.D(register_11_q), .Q(register_10_q), .clk(in_1), .clr(reset));  // open: en
  assign out_14 = 32'h80000001 | register_10_q;  // OR_Gate or_10, 32 bits wide
  Register #(.width(32)) register_11 (.D(register_12_q), .Q(register_11_q), .clk(in_1), .clr(reset));  // open: en
  assign out_15 = 32'h80000001 | register_11_q;  // OR_Gate or_11, 32 bits wide
  Register #(.width(32)) register_12 (.D(register_13_q), .Q(register_12_q), .clk(in_1), .clr(reset));  // open: en
  assign out_16 = 32'h80000001 | register_12_q;  // OR_Gate or_12, 32 bits wide
  Register #(.width(32)) register_13 (.D(register_14_q), .Q(register_13_q), .clk(in_1), .clr(reset));  // open: en
  assign out_17 = 32'h80000001 | register_13_q;  // OR_Gate or_13, 32 bits wide
  Register #(.width(32)) register_14 (.D(register_15_q), .Q(register_14_q), .clk(in_1), .clr(reset));  // open: en
  assign out_18 = 32'h80000001 | register_14_q;  // OR_Gate or_14, 32 bits wide
  Register #(.width(32)) register_15 (.D(register_16_q), .Q(register_15_q), .clk(in_1), .clr(reset));  // open: en
  assign out_19 = 32'h80000001 | register_15_q;  // OR_Gate or_15, 32 bits wide
  Register #(.width(32)) register_16 (.D(register_17_q), .Q(register_16_q), .clk(in_1), .clr(reset));  // open: en
  assign out_20 = 32'h80000001 | register_16_q;  // OR_Gate or_16, 32 bits wide
  Register #(.width(32)) register_17 (.D(register_18_q), .Q(register_17_q), .clk(in_1), .clr(reset));  // open: en
  assign out_21 = 32'h80000001 | register_17_q;  // OR_Gate or_17, 32 bits wide
  Register #(.width(32)) register_18 (.D(register_19_q), .Q(register_18_q), .clk(in_1), .clr(reset));  // open: en
  assign out_22 = 32'h80000001 | register_18_q;  // OR_Gate or_18, 32 bits wide
  Register #(.width(32)) register_19 (.D(register_20_q), .Q(register_19_q), .clk(in_1), .clr(reset));  // open: en
  assign out_23 = 32'h80000001 | register_19_q;  // OR_Gate or_19, 32 bits wide
  Register #(.width(32)) register_20 (.D(register_21_q), .Q(register_20_q), .clk(in_1), .clr(reset));  // open: en
  assign out_24 = 32'h80000001 | register_20_q;  // OR_Gate or_20, 32 bits wide
  Register #(.width(32)) register_21 (.D(register_22_q), .Q(register_21_q), .clk(in_1), .clr(reset));  // open: en
  assign out_25 = 32'h80000001 | register_21_q;  // OR_Gate or_21, 32 bits wide
  Register #(.width(32)) register_22 (.D(register_23_q), .Q(register_22_q), .clk(in_1), .clr(reset));  // open: en
  assign out_26 = 32'h80000001 | register_22_q;  // OR_Gate or_22, 32 bits wide
  Register #(.width(32)) register_23 (.D(register_24_q), .Q(register_23_q), .clk(in_1), .clr(reset));  // open: en
  assign out_27 = 32'h80000001 | register_23_q;  // OR_Gate or_23, 32 bits wide
  Register #(.width(32)) register_24 (.D(register_25_q), .Q(register_24_q), .clk(in_1), .clr(reset));  // open: en
  assign out_28 = 32'h80000001 | register_24_q;  // OR_Gate or_24, 32 bits wide
  Register #(.width(32)) register_25 (.D(register_26_q), .Q(register_25_q), .clk(in_1), .clr(reset));  // open: en
  assign out_29 = 32'h80000001 | register_25_q;  // OR_Gate or_25, 32 bits wide
  Register #(.width(32)) register_26 (.D(register_27_q), .Q(register_26_q), .clk(in_1), .clr(reset));  // open: en
  assign out_30 = 32'h80000001 | register_26_q;  // OR_Gate or_26, 32 bits wide
  Register #(.width(32)) register_27 (.D(register_29_q), .Q(register_27_q), .clk(in_1), .clr(reset));  // open: en
  Register #(.width(32)) register_28 (.D(in), .Q(register_28_q), .clk(in_1), .clr(reset));  // open: en
  assign out_31 = 32'h80000001 | register_27_q;  // OR_Gate or_27, 32 bits wide
  Register #(.width(32)) register_29 (.D(register_30_q), .Q(register_29_q), .clk(in_1), .clr(reset));  // open: en
  assign out_32 = 32'h80000001 | register_29_q;  // OR_Gate or_28, 32 bits wide
  Register #(.width(32)) register_30 (.D(register_31_q), .Q(register_30_q), .clk(in_1), .clr(reset));  // open: en
  assign out_33 = 32'h80000001 | register_30_q;  // OR_Gate or_29, 32 bits wide
  Register #(.width(32)) register_31 (.D(register_32_q), .Q(register_31_q), .clk(in_1), .clr(reset));  // open: en
  assign out_34 = 32'h80000001 | register_31_q;  // OR_Gate or_30, 32 bits wide
  Register #(.width(32)) register_32 (.D(register_33_q), .Q(register_32_q), .clk(in_1), .clr(reset));  // open: en
  assign out_35 = 32'h80000001 | register_32_q;  // OR_Gate or_31, 32 bits wide
  Register #(.width(32)) register_33 (.D(register_28_q), .Q(register_33_q), .clk(in_1), .clr(reset));  // open: en
  assign out_36 = 32'h80000001 | register_33_q;  // OR_Gate or_32, 32 bits wide

  // Other names for the same wires on the sheet: nul = in_1
endmodule

module luboy (
  input  [31:0] a,
  input  [31:0] b,
  output out_3
);

  wire or_1_out, or_2_out;

  or or_1 (or_1_out, a[1], a[2], a[3], a[4], a[5], a[6], a[7], a[8], a[9], a[10], a[11], a[12], a[13], a[14], a[15], a[16], a[17], a[18], a[19], a[20], a[21], a[22], a[23], a[24], a[25], a[26], a[27], a[28], a[29], a[30]);
  or or_2 (or_2_out, b[1], b[2], b[3], b[4], b[5], b[6], b[7], b[8], b[9], b[10], b[11], b[12], b[13], b[14], b[15], b[16], b[17], b[18], b[19], b[20], b[21], b[22], b[23], b[24], b[25], b[26], b[27], b[28], b[29], b[30]);
  or or_3 (out_3, or_1_out, or_2_out);
endmodule

module \break  (
  input  [31:0] a,
  input  [31:0] b,
  output \break 
);

  wire and_1_out, and_2_out, and_3_out, and_4_out, and_5_out, and_6_out, and_7_out, and_8_out, and_9_out,
       and_10_out, and_11_out, and_12_out, and_13_out, and_14_out, and_15_out, and_16_out, and_17_out,
       and_18_out, and_19_out, and_20_out, and_21_out, and_22_out, and_23_out, and_24_out, and_25_out,
       and_26_out, and_27_out, and_28_out, and_29_out, and_30_out, and_31_out, and_32_out;

  and and_1 (and_1_out, a[0], b[0]);
  and and_2 (and_2_out, a[1], b[1]);
  and and_3 (and_3_out, a[2], b[2]);
  and and_4 (and_4_out, a[3], b[3]);
  and and_5 (and_5_out, a[4], b[4]);
  and and_6 (and_6_out, a[5], b[5]);
  and and_7 (and_7_out, a[6], b[6]);
  and and_8 (and_8_out, a[7], b[7]);
  and and_9 (and_9_out, a[8], b[8]);
  and and_10 (and_10_out, a[9], b[9]);
  and and_11 (and_11_out, a[10], b[10]);
  and and_12 (and_12_out, a[11], b[11]);
  and and_13 (and_13_out, a[12], b[12]);
  and and_14 (and_14_out, a[13], b[13]);
  and and_15 (and_15_out, a[14], b[14]);
  and and_16 (and_16_out, a[15], b[15]);
  and and_17 (and_17_out, a[16], b[16]);
  and and_18 (and_18_out, a[17], b[17]);
  and and_19 (and_19_out, a[18], b[18]);
  and and_20 (and_20_out, a[19], b[19]);
  and and_21 (and_21_out, a[20], b[20]);
  and and_22 (and_22_out, a[21], b[21]);
  and and_23 (and_23_out, a[22], b[22]);
  and and_24 (and_24_out, a[23], b[23]);
  and and_25 (and_25_out, a[24], b[24]);
  and and_26 (and_26_out, a[25], b[25]);
  and and_27 (and_27_out, a[26], b[26]);
  and and_28 (and_28_out, a[27], b[27]);
  and and_29 (and_29_out, a[28], b[28]);
  and and_30 (and_30_out, a[29], b[29]);
  and and_31 (and_31_out, a[30], b[30]);
  and and_32 (and_32_out, a[31], b[31]);
  or or_1 (\break , and_1_out, and_2_out, and_3_out, and_4_out, and_5_out, and_6_out, and_7_out, and_8_out, and_9_out, and_10_out, and_11_out, and_12_out, and_13_out, and_14_out, and_15_out, and_16_out, and_17_out, and_18_out, and_19_out, and_20_out, and_21_out, and_22_out, and_23_out, and_24_out, and_25_out, and_26_out, and_27_out, and_28_out, and_29_out, and_30_out, and_31_out, and_32_out);
endmodule
